// Logisim project Add_Sub - Model 1.circ as structural Verilog: 4 circuits, main circuit main
module main (
  input  Operation_Mode,
  input  A2,
  input  A1,
  input  A0,
  input  B2,
  input  B1,
  input  B0,
  output SignBit,
  output C2,
  output C1,
  output C0
);

  wire n2_bit_adder_1_comparator_bit, n2_bit_adder_1_sum2, n2_bit_adder_1_xor_realoperand_1,
       real_operand_1_real_operand;

  Rs_Complement Rs_Complement (
    .Real_Operand(real_operand_1_real_operand), .Comparator_Bit(n2_bit_adder_1_comparator_bit),
    .Sum2(n2_bit_adder_1_sum2), .Sum1(C0), .out_5(C1));
  Real_Operand real_operand_1 (
    .XOR_RealOperand_1(n2_bit_adder_1_xor_realoperand_1), .Operation_Indicator(Operation_Mode),
    .Real_Operand(real_operand_1_real_operand));  // open: XOR_Input_1, XOR_Input_2, XOR_Output_1_2, XOR_Input_3, XOR_Input_4, XOR_Output_3_4, XOR_Input_5, XOR_Input_6, XOR_Output_5_6
  _2_bit_Adder u_2_bit_adder_1 (
    .A1(A1), .A0(A0), .Real_Operand(real_operand_1_real_operand), .B1(B1), .B0(B0), .Sign_A(A2), .Sign_B(B2),
    .XOR_RealOperand_1(n2_bit_adder_1_xor_realoperand_1), .Comparator_Bit(n2_bit_adder_1_comparator_bit),
    .Sum3(C2), .Sum2(n2_bit_adder_1_sum2), .Sum1(C0));
  // _74151 74151_1: pin names not known; wires that end beside it: 1'b1, 1'b0, 1'b1, 1'b0, SignBit, 1'b0, 1'b0, 1'b1, 1'b1, 1'b0, A2, real_operand_1_real_operand, n2_bit_adder_1_comparator_bit, C0
endmodule

module _2_bit_Adder (
  input  A1,
  input  A0,
  input  Real_Operand,
  input  B1,
  input  B0,
  input  Sign_A,
  input  Sign_B,
  output XOR_RealOperand_1,
  output Comparator_Bit,
  output Sum3,
  output Sum2,
  output Sum1
);

  wire n7483_1_p1, n7483_1_p8, n7486_1_p1, n7486_1_p15;

  // _7483 7483_1: pin names not known; wires that end beside it: n7483_1_p1, 1'b0, 1'b0, 1'b1, Sum2, Real_Operand, 1'b0, n7483_1_p8
  // _7486 7486_1: pin names not known; wires that end beside it: n7486_1_p1, A1, B0, Real_Operand, n7483_1_p8, B1, Real_Operand, n7486_1_p1, 1'b0, A0, Sum1, 1'b1, Real_Operand, 1'b1, n7486_1_p15, Sign_B, Sign_A, XOR_RealOperand_1
  // _7408 7408_1: pin names not known; wires that end beside it: n7483_1_p1, n7486_1_p15, Sum3, 1'b0, 1'b1
  // comparator_4_bit_mag_main main_1: pin names not known; wires that end beside it: 1'b0, 1'b0, 1'b0, 1'b0, 1'b1, 1'b1, 1'b1, A1, B1, A0, B0, Comparator_Bit
endmodule

module Real_Operand (
  input  XOR_RealOperand_1,
  input  Operation_Indicator,
  input  XOR_Input_1,
  input  XOR_Input_2,
  input  XOR_Input_3,
  input  XOR_Input_4,
  input  XOR_Input_5,
  input  XOR_Input_6,
  output XOR_Output_1_2,
  output XOR_Output_3_4,
  output XOR_Output_5_6,
  output Real_Operand
);

  // _7486 7486_1: pin names not known; wires that end beside it: Operation_Indicator, XOR_RealOperand_1, Real_Operand, XOR_Input_5, XOR_Input_6, XOR_Output_5_6, 1'b0, 1'b1, XOR_Input_1, XOR_Input_2, XOR_Output_1_2, XOR_Input_3, XOR_Input_4, XOR_Output_3_4
endmodule

module Rs_Complement (
  input  Real_Operand,
  input  Comparator_Bit,
  input  Sum2,
  input  Sum1,
  output out_5
);

  wire n74151_1_p7;

  // _74151 74151_1: pin names not known; wires that end beside it: 1'b1, 1'b0, out_5, 1'b0, Real_Operand, 1'b1, n74151_1_p7, Sum1
  // _7404 7404_1: pin names not known; wires that end beside it: 1'b0, Real_Operand, n74151_1_p7, 1'b0, Sum2, Comparator_Bit, 1'b1
endmodule
