// Logisim project Integration Circuit - Model 1.circ as structural Verilog
module Integration (
  input  A2,
  input  A1,
  input  A0,
  input  Operation_Mode__1,
  input  Operation_Mode__0,
  input  B2,
  input  B1,
  input  B0,
  output Sign,
  output Out_3,
  output Out_2,
  output Out_1,
  output Out_1_2
);

  wire main_1_c0, main_1_c1, main_1_c2, main_1_signbit, multiplier_1_p0, multiplier_1_p1, multiplier_1_p2,
       multiplier_1_p3, multiplier_1_sign_bit, remainder_1_r0, remainder_1_r1, remainder_1_sign_bit;

  Add_Sub___Model_1_main main_1 (
    .A2(A2), .A1(A1), .A0(A0), .Operation_Mode(Operation_Mode__0), .B2(B2), .B1(B1), .B0(B0),
    .SignBit(main_1_signbit), .C2(main_1_c2), .C1(main_1_c1), .C0(main_1_c0));
  _744052_main main_2 (
    ._2Y0(main_1_signbit), ._2Y2(multiplier_1_sign_bit), ._2Z(Sign), ._2Y3(remainder_1_sign_bit),
    ._2Y1(main_1_signbit), .S0(Operation_Mode__0), .S1(Operation_Mode__1));  // open: E, VEE, GND, Vcc, _1Y2, _1Y1, _1Z, _1Y0, _1Y3
  Remainder remainder_1 (
    .A2(A2), .A1(A1), .A0(A0), .B2(B2), .B1(B1), .B0(B0), .Sign_Bit(remainder_1_sign_bit),
    .R1(remainder_1_r1), .R0(remainder_1_r0));
  Multiplier multiplier_1 (
    .A2(A2), .A1(A1), .A0(A0), .B2(B2), .B1(B1), .B0(B0), .Sign_Bit(multiplier_1_sign_bit),
    .P3(multiplier_1_p3), .P2(multiplier_1_p2), .P1(multiplier_1_p1), .P0(multiplier_1_p0));  // open: AND_Input_1, AND_Input_2, AND_Output_1_2, AND_Input_3, AND_Input_4, AND_Output_3_4, XOR_Input_1, XOR_Input_2, XOR_Output_1_2
  _744052_main main_3 (
    ._2Y0(main_1_c1), ._2Y2(multiplier_1_p1), ._2Z(Out_1), ._2Y3(remainder_1_r1), ._2Y1(main_1_c1),
    .GND(1'b0), .Vcc(1'b1), ._1Y2(multiplier_1_p0), ._1Y1(main_1_c0), ._1Z(Out_1_2), ._1Y0(main_1_c0),
    ._1Y3(remainder_1_r0), .S0(Operation_Mode__0), .S1(Operation_Mode__1));  // open: E, VEE
  _744052_main main_4 (
    ._2Y0(1'b0), ._2Y2(multiplier_1_p3), ._2Z(Out_3), ._2Y3(1'b0), ._2Y1(1'b0), .GND(1'b0), .Vcc(1'b1),
    ._1Y2(multiplier_1_p2), ._1Y1(main_1_c2), ._1Z(Out_2), ._1Y0(main_1_c2), ._1Y3(1'b0),
    .S0(Operation_Mode__0), .S1(Operation_Mode__1));  // open: E, VEE
endmodule
