// Logisim project Multiplier.circ as structural Verilog: 2 circuits, main circuit Multiplier
module Multiplier (
  input  A2,
  input  A1,
  input  A0,
  input  B2,
  input  B1,
  input  B0,
  input  AND_Input_1,
  input  AND_Input_2,
  input  AND_Input_3,
  input  AND_Input_4,
  input  XOR_Input_1,
  input  XOR_Input_2,
  output AND_Output_1_2,
  output AND_Output_3_4,
  output XOR_Output_1_2,
  output Sign_Bit,
  output P3,
  output P2,
  output P1,
  output P0
);

  wire n7408_1_p9, n7408_2_p1, n7408_2_p3, n7408_2_p5;

  // _7408 7408_1: pin names not known; wires that end beside it: B0, A0, P0, B1, A0, 1'b1, B1, A1, n7408_1_p9, B0
  // _7408 7408_2: pin names not known; wires that end beside it: n7408_2_p1, 1'b0, n7408_2_p3, n7408_2_p1, n7408_2_p5, n7408_1_p9, n7408_2_p5, P3, A1, n7408_2_p3, 1'b1, AND_Input_1, AND_Input_2, AND_Output_1_2, AND_Input_3, AND_Input_4
  // _7486 7486_1: pin names not known; wires that end beside it: 1'b0, n7408_2_p3, n7408_2_p1, P1, n7408_2_p5, n7408_1_p9, P2, 1'b0, AND_Output_3_4, 1'b1, B2, A2, Sign_Bit, XOR_Input_1, XOR_Input_2, XOR_Output_1_2
endmodule

module MultiplierOPT (
  input  A2,
  input  A1,
  input  A0,
  input  B2,
  input  B1,
  input  B0,
  input  AND_Input_1,
  input  AND_Input_2,
  input  AND_Input_3,
  input  AND_Input_4,
  input  XOR_Input_1,
  input  XOR_Input_2,
  output AND_Output_1_2,
  output AND_Output_3_4,
  output XOR_Output_1_2,
  output Sign_Bit,
  output P3,
  output P2,
  output P1,
  output P0
);

  wire n7408_1_p9, n7408_2_p1, n7408_2_p3, n7408_2_p5;

  // _7408 7408_1: pin names not known; wires that end beside it: B0, A0, P0, B1, A0, 1'b1, B1, A1, n7408_1_p9, B0
  // _7408 7408_2: pin names not known; wires that end beside it: n7408_2_p1, 1'b0, n7408_2_p3, n7408_2_p1, n7408_2_p5, n7408_1_p9, n7408_2_p5, P3, A1, n7408_2_p3, 1'b1, AND_Input_1, AND_Input_2, AND_Output_1_2, AND_Input_3, AND_Input_4
  // _7486 7486_1: pin names not known; wires that end beside it: 1'b0, n7408_2_p3, n7408_2_p1, P1, n7408_2_p5, n7408_1_p9, P2, 1'b0, AND_Output_3_4, 1'b1, B2, A2, Sign_Bit, XOR_Input_1, XOR_Input_2, XOR_Output_1_2
endmodule
