// Logisim project Remainder.circ as structural Verilog: 1 circuit, main circuit Remainder
module Remainder (
  input  A2,
  input  A1,
  input  A0,
  input  B2,
  input  B1,
  input  B0,
  output Sign_Bit,
  output R1,
  output R0
);

  wire multiplier_1_p1, n7408_1_p4, n7408_1_p7, n7408_1_p10, n7408_1_p12;

  // Multiplier multiplier_1: pin names not known; wires that end beside it: multiplier_1_p1, A0, R0
  // _7408 7408_1: pin names not known; wires that end beside it: B2, A1, B0, n7408_1_p4, n7408_1_p4, B1, n7408_1_p7, 1'b1, n7408_1_p7, n7408_1_p10, R1, n7408_1_p12, B1
  // _7404 7404_1: pin names not known; wires that end beside it: 1'b0, n7408_1_p4, n7408_1_p12, A0, n7408_1_p10, 1'b0, multiplier_1_p1, 1'b1

  assign Sign_Bit = A2;
endmodule
