// Logisim project mux-4-to-1.circ as structural Verilog: 1 circuit, main circuit main
module main (
  input  MSB,
  input  LSB,
  input  A,
  input  B,
  input  C,
  input  D,
  output out_7
);

  wire _00_out, _01_out, _10_out, _11_out, not_1_out, not_2_out;

  not not_1 (not_1_out, LSB);
  not not_2 (not_2_out, MSB);
  nand _00 (_00_out, not_1_out, not_2_out, A);
  nand _01 (_01_out, not_2_out, LSB, B);
  nand _10 (_10_out, MSB, not_1_out, C);
  nand _11 (_11_out, LSB, MSB, D);
  nand nand_1 (out_7, _00_out, _01_out, _10_out, _11_out);

  // Notes on the sheet:
  //   Address
  //   4 to 1 Multiplexer
  //   www.learnabout-electronics.org
  //   Suggestion for a Practical Project:
  //   Modify this circuit to make an 8 to1 Multiplexer
  //   (Get some clues to how it would look by studying  datasheets)
endmodule
