// Logisim project 744052.circ as structural Verilog: 1 circuit, main circuit main
module main (
  input  _2Y0,
  input  Vcc,
  input  _2Y2,
  input  _1Y2,
  input  _1Y1,
  input  _2Y3,
  input  _2Y1,
  input  _1Y0,
  input  E,
  input  _1Y3,
  input  VEE,
  input  S0,
  input  GND,
  input  S1,
  output _2Z,
  output _1Z
);

  mux_4_to_1_main main_1 (.A(_2Y0), .B(_2Y1), .C(_2Y2), .D(_2Y3), .MSB(S1), .LSB(S0), .out_7(_2Z));
  mux_4_to_1_main main_2 (.A(_1Y0), .B(_1Y1), .C(_1Y2), .D(_1Y3), .MSB(S1), .LSB(S0), .out_7(_1Z));
endmodule
