// Logisim project Adder_Subtractor - Model 2.circ as structural Verilog: 4 circuits, main circuit Addition/Subtract
module Addition_Subtract (
  input  Operation_Mode,
  input  XOR_Input_1,
  input  A2,
  input  A1,
  input  A0,
  input  B2,
  input  B1,
  input  B0,
  input  XOR_Input_2,
  input  XOR_Input_3,
  input  XOR_Input_4,
  input  XOR_Input_5,
  input  XOR_Input_6,
  input  AND_Input_1,
  input  AND_Input_2,
  input  AND_Input_3,
  input  AND_Input_4,
  input  AND_Input_5,
  input  AND_Input_6,
  input  NOT_Input_1,
  input  NOT_Input_2,
  input  NOT_Input_3,
  input  NOT_Input_4,
  input  NOT_Input_5,
  output XOR_Output_1_2,
  output XOR_Output_3_4,
  output XOR_Output_5_6,
  output AND_Output_1_2,
  output AND_Output_3_4,
  output AND_Output_5_6,
  output NOT_Output_1,
  output NOT_Output_2,
  output NOT_Output_3,
  output NOT_Output_4,
  output Add_Sub_SignBit,
  output C2,
  output C1,
  output C0,
  output NOT_Output_5
);

  wire n2_bit_adder_1_sum2, n2_bit_adder_1_xor_realoperand_1, n74151_1_p11, n74151_1_p12;

  // _74151 74151_1: pin names not known; wires that end beside it: 1'b1, 1'b0, 1'b1, 1'b0, 1'b0, 1'b0, 1'b1, 1'b1, Add_Sub_SignBit, A2, n74151_1_p11, n74151_1_p12
  Real_Operand real_operand_1 (
    .XOR_RealOperand_1(n2_bit_adder_1_xor_realoperand_1), .Operation_Indicator(Operation_Mode),
    .Real_Operand(n74151_1_p11), .XOR_Input_1(XOR_Input_1), .XOR_Input_2(XOR_Input_2),
    .XOR_Output_1_2(XOR_Output_1_2), .XOR_Input_3(XOR_Input_3), .XOR_Input_4(XOR_Input_4),
    .XOR_Output_3_4(XOR_Output_3_4), .XOR_Input_5(XOR_Input_5), .XOR_Input_6(XOR_Input_6),
    .XOR_Output_5_6(XOR_Output_5_6));
  _2_Bit_Adder u_2_bit_adder_1 (
    .A1(A1), .A0(A0), .Real_Operand(n74151_1_p11), .B1(B1), .B0(B0), .Sign_A(A2), .Sign_B(B2),
    .XOR_RealOperand_1(n2_bit_adder_1_xor_realoperand_1), .Comparator_Bit(n74151_1_p12), .Sum3(C2),
    .Sum2(n2_bit_adder_1_sum2), .Sum1(C0), .AND_Input_1(AND_Input_1), .AND_Input_2(AND_Input_2),
    .AND_Output_1_2(AND_Output_1_2), .AND_Input_3(AND_Input_3), .AND_Input_4(AND_Input_4),
    .AND_Output_3_4(AND_Output_3_4), .AND_Input_5(AND_Input_5), .AND_Input_6(AND_Input_6),
    .AND_Output_5_6(AND_Output_5_6));
  Rs_Complement rs_complement_1 (
    .Real_Operand(n74151_1_p11), .Comparator_Bit(n74151_1_p12), .Sum2(n2_bit_adder_1_sum2), .Sum1(C0),
    .Sum2_2(C1), .NOT_Input_1(NOT_Input_1), .NOT_Output_1(NOT_Output_1), .NOT_Input_2(NOT_Input_2),
    .NOT_Output_2(NOT_Output_2), .NOT_Input_3(NOT_Input_3), .NOT_Output_3(NOT_Output_3),
    .NOT_Input_4(NOT_Input_4), .NOT_Output_4(NOT_Output_4), .NOT_Input_5(NOT_Input_5),
    .NOT_Output_5(NOT_Output_5));

  // Notes on the sheet:
  //   Comment: This is the Addition/Subtraction Circuit
  //   Comment: Outputs are SignBit, C2, C1, C0 at the bottom left of the page
  //   Comment: The inputs and outputs on the right are used for optimisation of other circuits
endmodule

module _2_Bit_Adder (
  input  A1,
  input  A0,
  input  Real_Operand,
  input  B1,
  input  B0,
  input  Sign_A,
  input  Sign_B,
  input  AND_Input_1,
  input  AND_Input_2,
  input  AND_Input_3,
  input  AND_Input_4,
  input  AND_Input_5,
  input  AND_Input_6,
  output XOR_RealOperand_1,
  output Comparator_Bit,
  output Sum3,
  output Sum2,
  output Sum1,
  output AND_Output_1_2,
  output AND_Output_3_4,
  output AND_Output_5_6
);

  wire n7483_1_p1, n7483_1_p8, n7486_1_p1, n7486_1_p15;

  // _7483 7483_1: pin names not known; wires that end beside it: n7483_1_p1, 1'b0, 1'b0, 1'b1, Sum2, Real_Operand, 1'b0, n7483_1_p8
  // _7486 7486_1: pin names not known; wires that end beside it: n7486_1_p1, A1, B0, Real_Operand, n7483_1_p8, B1, Real_Operand, n7486_1_p1, 1'b0, A0, Sum1, 1'b1, Real_Operand, 1'b1, n7486_1_p15, Sign_B, Sign_A, XOR_RealOperand_1
  // _7408 7408_1: pin names not known; wires that end beside it: n7483_1_p1, n7486_1_p15, Sum3, AND_Input_1, AND_Input_2, AND_Output_1_2, 1'b0, 1'b1, AND_Input_4, AND_Input_3, AND_Output_3_4, AND_Input_5, AND_Input_6, AND_Output_5_6
  // comparator_4_bit_mag_main main_1: pin names not known; wires that end beside it: 1'b0, 1'b0, 1'b0, 1'b0, 1'b1, 1'b1, 1'b1, A1, B1, A0, B0, Comparator_Bit
endmodule

module Real_Operand (
  input  XOR_RealOperand_1,
  input  Operation_Indicator,
  input  XOR_Input_1,
  input  XOR_Input_2,
  input  XOR_Input_3,
  input  XOR_Input_4,
  input  XOR_Input_5,
  input  XOR_Input_6,
  output XOR_Output_1_2,
  output XOR_Output_3_4,
  output XOR_Output_5_6,
  output Real_Operand
);

  // _7486 7486_1: pin names not known; wires that end beside it: Operation_Indicator, XOR_RealOperand_1, Real_Operand, XOR_Input_5, XOR_Input_6, XOR_Output_5_6, 1'b0, 1'b1, XOR_Input_1, XOR_Input_2, XOR_Output_1_2, XOR_Input_3, XOR_Input_4, XOR_Output_3_4
endmodule

module Rs_Complement (
  input  Real_Operand,
  input  Comparator_Bit,
  input  Sum2,
  input  Sum1,
  input  NOT_Input_1,
  input  NOT_Input_2,
  input  NOT_Input_3,
  input  NOT_Input_4,
  input  NOT_Input_5,
  output NOT_Output_1,
  output NOT_Output_2,
  output NOT_Output_3,
  output NOT_Output_4,
  output NOT_Output_5,
  output Sum2_2
);

  wire n74151_1_p7;

  // _74151 74151_1: pin names not known; wires that end beside it: 1'b1, 1'b0, Sum2_2, 1'b0, Real_Operand, 1'b1, n74151_1_p7, Sum1
  // _7404 7404_1: pin names not known; wires that end beside it: 1'b0, Real_Operand, n74151_1_p7, NOT_Input_4, NOT_Output_4, NOT_Input_5, NOT_Output_5, 1'b0, Sum2, Comparator_Bit, 1'b1, NOT_Input_1, NOT_Output_1, NOT_Input_2, NOT_Output_2, NOT_Input_3, NOT_Output_3
endmodule
