// Logisim project Integrated Circuit - Optimised.circ as structural Verilog: 2 circuits, main circuit Integrated Circuit
module Integrated_Circuit (
  input  A2,
  input  A1,
  input  A0,
  input  Operation_Mode_1,
  input  Operation_Mode_0,
  input  B2,
  input  B1,
  input  B0
);

  wire addition_subtract_1_add_sub_signbit, addition_subtract_1_c0, addition_subtract_1_c1,
       addition_subtract_1_c2, addition_subtract_1_not_output_3, addition_subtract_1_not_output_4,
       addition_subtract_1_not_output_5, multiplier_1_p0, multiplier_1_p1, multiplier_1_p2, multiplier_1_p3,
       multiplier_1_sign, n7408_1_p3, n7408_1_p6, n7408_1_p10, n7408_1_p11, n7432_1_p4, n7432_1_p7,
       n7432_1_p9, n7448_1_p9, n7448_1_p10, n7448_1_p11, n7448_1_p12, n7448_1_p13, n7448_1_p14, n7448_1_p15,
       remainder_1_r0, remainder_1_r1, remainder_1_remainder_signbit, selector_1_out0, selector_1_out1,
       selector_1_out2, selector_1_out3, selector_1_signbit;

  Addition_Subtract addition_subtract_1 (
    .A2(A2), .A1(A1), .A0(A0), .Operation_Mode(Operation_Mode_0), .B2(B2), .B1(B1), .B0(B0),
    .Add_Sub_SignBit(addition_subtract_1_add_sub_signbit), .C2(addition_subtract_1_c2),
    .C1(addition_subtract_1_c1), .C0(addition_subtract_1_c0), .NOT_Input_3(B1),
    .NOT_Output_3(addition_subtract_1_not_output_3), .NOT_Input_4(B0),
    .NOT_Output_4(addition_subtract_1_not_output_4), .NOT_Input_5(n7408_1_p11),
    .NOT_Output_5(addition_subtract_1_not_output_5));  // open: XOR_Input_1, XOR_Input_2, XOR_Output_1_2, XOR_Input_3, XOR_Input_4, XOR_Output_3_4, XOR_Input_5, XOR_Input_6, XOR_Output_5_6, AND_Input_1, AND_Input_2, AND_Output_1_2, AND_Input_3, AND_Input_4, AND_Output_3_4, AND_Input_5, AND_Input_6, AND_Output_5_6, NOT_Input_1, NOT_Output_1, NOT_Input_2, NOT_Output_2
  Multiplier multiplier_1 (
    .A2(A2), .A1(A1), .A0(A0), .B2(B2), .B1(B1), .B0(B0), .Sign(multiplier_1_sign), .P3(multiplier_1_p3),
    .P2(multiplier_1_p2), .P1(multiplier_1_p1), .P0(multiplier_1_p0));
  Remainder remainder_1 (
    .A2(A2), .A1(A1), .A0(A0), .B2(B2), .B1(B1), .B0(B0), .Remainder_SignBit(remainder_1_remainder_signbit),
    .R1(remainder_1_r1), .R0(remainder_1_r0));
  Selector selector_1 (
    .C0(addition_subtract_1_c0), .C1(addition_subtract_1_c1), .C2(addition_subtract_1_c2),
    .Add_Sub_SignBit(addition_subtract_1_add_sub_signbit), .P0(multiplier_1_p0), .P1(multiplier_1_p1),
    .P2(multiplier_1_p2), .P3(multiplier_1_p3), .Multiplier_SignBit(multiplier_1_sign), .R0(remainder_1_r0),
    .R1(remainder_1_r1), .Remainder_SignBit(remainder_1_remainder_signbit),
    .Operation_Mode_1(Operation_Mode_1), .Operation_Mode_0(Operation_Mode_0), .SignBit(selector_1_signbit),
    .Out3(selector_1_out3), .Out2(selector_1_out2), .Out1(selector_1_out1), .Out0(selector_1_out0));
  // _7408 7408_1: pin names not known; wires that end beside it: addition_subtract_1_not_output_3, addition_subtract_1_not_output_4, n7408_1_p3, Operation_Mode_1, Operation_Mode_0, n7408_1_p6, 1'b1, n7408_1_p3, n7408_1_p6, n7408_1_p10, n7408_1_p11, selector_1_signbit
  // _7432 7432_1: pin names not known; wires that end beside it: 1'b0, selector_1_out0, selector_1_out1, n7432_1_p4, selector_1_out2, selector_1_out3, n7432_1_p7, 1'b0, n7432_1_p9, 1'b1, n7432_1_p4, n7432_1_p7, n7408_1_p11
  LED Zero_Flag (.in(addition_subtract_1_not_output_5));
  // _7448 7448_1: pin names not known; wires that end beside it: selector_1_out1, selector_1_out2, 1'b1, 1'b1, 1'b1, selector_1_out3, selector_1_out0, 1'b0, n7448_1_p9, n7448_1_p10, n7448_1_p11, n7448_1_p12, n7448_1_p13, n7448_1_p14, n7448_1_p15
  LED Div_Zero_flag (.in(n7408_1_p10));
  _7_Segment_Display u_7_segment_display_1 (.g(n7432_1_p9));  // open: f, a, b, e, d, c, dp
  LED Sign_Flag (.in(selector_1_signbit));
  _7_Segment_Display u_7_segment_display_2 (
    .g(n7448_1_p10), .f(n7448_1_p9), .a(n7448_1_p11), .b(n7448_1_p12), .e(n7448_1_p15), .d(n7448_1_p14),
    .c(n7448_1_p13));  // open: dp

  // Notes on the sheet:
  //   Addition/Subtraction
  //   Multiplier
  //   Operation Mode:
  //   1) Add - 0 0
  //   2) Subtract - 0 1
  //   3) Multiply - 1 0
  //   4) Remainder - 1 1
  //   Flags Off Colour:
  //   - Black
  //   Remainder
endmodule

module Selector (
  input  Operation_Mode_1,
  input  Operation_Mode_0,
  input  C0,
  input  C1,
  input  C2,
  input  Add_Sub_SignBit,
  input  P0,
  input  P1,
  input  P2,
  input  P3,
  input  Multiplier_SignBit,
  input  R0,
  input  R1,
  input  Remainder_SignBit,
  output SignBit,
  output Out3,
  output Out2,
  output Out1,
  output Out0
);

  _744052_main main_1 (
    ._2Y0(C1), ._2Y2(P1), ._2Z(Out1), ._2Y3(R1), ._2Y1(C1), .GND(1'b0), .Vcc(1'b1), ._1Y2(P0), ._1Y1(C0),
    ._1Z(Out0), ._1Y0(C0), ._1Y3(R0), .S0(Operation_Mode_0), .S1(Operation_Mode_1));  // open: E, VEE
  _744052_main main_2 (
    ._2Y0(Add_Sub_SignBit), ._2Y2(Multiplier_SignBit), ._2Z(SignBit), ._2Y3(Remainder_SignBit),
    ._2Y1(Add_Sub_SignBit), .GND(1'b0), .Vcc(1'b1), ._1Y2(P2), ._1Y1(C2), ._1Z(Out2), ._1Y0(C2), ._1Y3(1'b0),
    .S0(Operation_Mode_0), .S1(Operation_Mode_1));  // open: E, VEE
  _744052_main main_3 (
    ._2Y0(1'b0), ._2Y2(P3), ._2Z(Out3), ._2Y3(1'b0), ._2Y1(1'b0), .GND(1'b0), .Vcc(1'b1),
    .S0(Operation_Mode_0), .S1(Operation_Mode_1));  // open: E, VEE, _1Y2, _1Y1, _1Z, _1Y0, _1Y3

  // Notes on the sheet:
  //   Add/Sub Out Bits
  //   Multiplier Out Bits
  //   Remainder Out Bits
endmodule
