// Logisim project Multiplier - Model 2.circ as structural Verilog: 1 circuit, main circuit Multiplier
module Multiplier (
  input  A2,
  input  A1,
  input  A0,
  input  B2,
  input  B1,
  input  B0,
  output Sign,
  output P3,
  output P2,
  output P1,
  output P0
);

  wire addition_subtract_1_and_output_1_2, addition_subtract_1_and_output_3_4, n7408_1_p6, n7408_1_p11;

  Addition_Subtract addition_subtract_1 (
    .XOR_Input_1(n7408_1_p6), .XOR_Input_2(n7408_1_p11), .XOR_Output_1_2(P1),
    .XOR_Input_3(addition_subtract_1_and_output_3_4), .XOR_Input_4(addition_subtract_1_and_output_1_2),
    .XOR_Output_3_4(P2), .XOR_Input_5(A2), .XOR_Input_6(B2), .XOR_Output_5_6(Sign), .AND_Input_1(n7408_1_p6),
    .AND_Input_2(n7408_1_p11), .AND_Output_1_2(addition_subtract_1_and_output_1_2), .AND_Input_3(B1),
    .AND_Input_4(A1), .AND_Output_3_4(addition_subtract_1_and_output_3_4));  // open: A2, A1, A0, Operation_Mode, B2, B1, B0, Add_Sub_SignBit, C2, C1, C0, AND_Input_5, AND_Input_6, AND_Output_5_6, NOT_Input_1, NOT_Output_1, NOT_Input_2, NOT_Output_2, NOT_Input_3, NOT_Output_3, NOT_Input_4, NOT_Output_4, NOT_Input_5, NOT_Output_5
  // _7408 7408_1: pin names not known; wires that end beside it: A0, B0, P0, A0, B1, n7408_1_p6, 1'b0, 1'b1, B0, A1, n7408_1_p11, addition_subtract_1_and_output_3_4, addition_subtract_1_and_output_1_2, P3

  // Notes on the sheet:
  //   Comment: This is the Multiplier Circuit
  //   Comment: The ouputs are P0, P1, P2, P3 and SignBit
  //   presented at the right bottom of the circuit
  //   Comment: There are empty gates at the Add/Sub circuit we've used it
  //   are AND and which are XOR hoover over each node
  //   for optimisation, hoover over the node of each wire to know which
endmodule
