// Logisim project Remainder - Model 2.circ as structural Verilog: 1 circuit, main circuit Remainder
module Remainder (
  input  A2,
  input  A1,
  input  A0,
  input  B2,
  input  B1,
  input  B0,
  output Remainder_SignBit,
  output R1,
  output R0
);

  wire addition_subtract_1_not_output_1, addition_subtract_1_not_output_2, n7408_1_p3, n7408_1_p6,
       n7408_1_p13;

  Addition_Subtract addition_subtract_1 (
    .AND_Input_5(n7408_1_p13), .AND_Input_6(A1), .AND_Output_5_6(R1), .NOT_Input_1(n7408_1_p3),
    .NOT_Output_1(addition_subtract_1_not_output_1), .NOT_Input_2(A0),
    .NOT_Output_2(addition_subtract_1_not_output_2));  // open: A2, A1, A0, Operation_Mode, B2, B1, B0, Add_Sub_SignBit, C2, C1, C0, XOR_Input_1, XOR_Input_2, XOR_Output_1_2, XOR_Input_3, XOR_Input_4, XOR_Output_3_4, XOR_Input_5, XOR_Input_6, XOR_Output_5_6, AND_Input_1, AND_Input_2, AND_Output_1_2, AND_Input_3, AND_Input_4, AND_Output_3_4, NOT_Input_3, NOT_Output_3, NOT_Input_4, NOT_Output_4, NOT_Input_5, NOT_Output_5
  // _7408 7408_1: pin names not known; wires that end beside it: A1, B0, n7408_1_p3, addition_subtract_1_not_output_1, B1, n7408_1_p6, 1'b1, n7408_1_p6, A0, R0, n7408_1_p3, addition_subtract_1_not_output_2, n7408_1_p13

  assign Remainder_SignBit = A2;

  // Notes on the sheet:
  //   Comment: This is the Remainder Circuit
  //   Comment: we've used empty gates from the Add/Sub circuit for optimisation
endmodule
